// Logisim project 3 Bit Logic Gate Counter.circ as structural Verilog: 1 circuit, main circuit main
module main (
  input  Threshold,
  input  in_2,
  input  in_3,
  output out_4,
  output out_5,
  output out_6
);

  wire A_qn, and_1_out, and_2_out, and_3_out, and_4_out, and_5_out, and_6_out, and_7_out, and_8_out,
       and_9_out, and_10_out, and_11_out, and_12_out, and_13_out, B_qn, button_1_out, button_2_out,
       nor_1_out, nor_2_out, not_1_out, not_2_out, not_3_out, not_4_out, not_5_out, not_6_out, not_7_out,
       not_8_out, not_9_out, or_1_out, or_2_out, or_3_out, or_4_out, xnor_1_out, xnor_2_out, xnor_3_out,
       xnor_4_out, xnor_5_out, xnor_6_out;

  Button button_1 (.out(button_1_out));
  Button button_2 (.out(button_2_out));
  nor nor_1 (nor_1_out, button_1_out, nor_2_out);
  nor nor_2 (nor_2_out, nor_1_out, button_2_out);
  not not_1 (not_1_out, not_2_out);
  or or_1 (or_1_out, button_1_out, button_2_out);
  not not_2 (not_2_out, or_1_out);
  not not_3 (not_3_out, not_4_out);
  not not_4 (not_4_out, not_1_out);
  T_Flip_Flop A (.clk(not_3_out), .T(1'b1), .Q(out_6), .Qn(A_qn));  // open: preset, reset, en
  and and_1 (and_1_out, nor_1_out, out_6);
  and and_2 (and_2_out, A_qn, nor_2_out);
  or or_2 (or_2_out, and_1_out, and_2_out);
  xnor xnor_1 (xnor_1_out, out_5, in_2);
  xnor xnor_2 (xnor_2_out, out_4, Threshold);
  and and_3 (and_3_out, out_6, not_5_out);
  not not_5 (not_5_out, in_3);
  and and_4 (and_4_out, out_4, not_6_out);
  not not_6 (not_6_out, Threshold);
  and and_5 (and_5_out, out_5, not_7_out);
  not not_7 (not_7_out, in_2);
  xnor xnor_3 (xnor_3_out, out_6, in_3);
  and and_6 (and_6_out, in_3, not_8_out);
  not not_8 (not_8_out, out_6);
  T_Flip_Flop B (.clk(not_3_out), .T(or_2_out), .Q(out_5), .Qn(B_qn));  // open: preset, reset, en
  and and_7 (and_7_out, xnor_1_out, xnor_2_out);
  and and_8 (and_8_out, xnor_2_out, and_5_out);
  not not_9 (not_9_out, and_6_out);
  and and_9 (and_9_out, and_1_out, out_5);
  and and_10 (and_10_out, B_qn, and_2_out);
  and and_11 (and_11_out, and_7_out, and_3_out);
  xnor xnor_4 (xnor_4_out, and_4_out, and_8_out);
  and and_12 (and_12_out, and_7_out, xnor_3_out);
  and and_13 (and_13_out, and_7_out, not_9_out);
  or or_3 (or_3_out, and_8_out, and_4_out);
  or or_4 (or_4_out, and_9_out, and_10_out);
  xnor xnor_5 (xnor_5_out, and_11_out, xnor_4_out);
  LED led_1 (.in(xnor_5_out));
  xnor xnor_6 (xnor_6_out, and_13_out, or_3_out);
  T_Flip_Flop C (.clk(not_3_out), .T(or_4_out), .Q(out_4));  // open: Qn, preset, reset, en

  // Notes on the sheet:
  //   Count Down
  //   Count Up
  //   Counter Output
  //   Turn on if exceed threshold
endmodule
